# Fritzing sketch Plan (saved by Fritzing 0.9.10b)
circuit board: 8.46667cm x 5.64444cm
breadboards: 1

parts:
  WeMos_D1_Mini1 = WeMos D1 Mini
  microSD1 = MicroSD Card Module
  ZS-042_RTC1 = ZS-042 RTC Module
  DHT11 = Humidity and Temperature Sensor RHT03
  CCS811 = I2C level shifter bidirectional

nets:
  3V3: WeMos_D1_Mini1.3V3, ZS-042_RTC1.VCC, CCS811.LV
  VCC: WeMos_D1_Mini1.5V, microSD1.VCC, DHT11.Vcc, CCS811.HV
  N1: WeMos_D1_Mini1.D1, ZS-042_RTC1.SDA, CCS811.LV1
  N2: WeMos_D1_Mini1.D2, ZS-042_RTC1.SCL, CCS811.LV4
  N3: WeMos_D1_Mini1.D4, DHT11.Data-signal
  N4: WeMos_D1_Mini1.D5, microSD1.SCK
  N5: WeMos_D1_Mini1.D6, microSD1.MISO
  N6: WeMos_D1_Mini1.D7, microSD1.MOSI
  N7: WeMos_D1_Mini1.D8, microSD1.CS
  N8: WeMos_D1_Mini1.G, microSD1.GND, DHT11.GND_1
