# Fritzing sketch Wiring (saved by Fritzing 0.9.10b)

parts:
  WeMos_D1_Mini1 = WeMos D1 Mini
  microSD1 = MicroSD Card Module
  LED1 = smd LED [color="Red (633nm)" package="1206 [SMD]"]  # not connected
  LED2 = smd LED [color="Red (633nm)" package="1206 [SMD]"]  # not connected
  LED3 = smd LED [color="Red (633nm)" package="1206 [SMD]"]  # not connected
  ZS-042_RTC1 = ZS-042 RTC Module
  RHT1 = Humidity and Temperature Sensor RHT03

nets:
  3V3: WeMos_D1_Mini1.3V3, ZS-042_RTC1.VCC
  VCC: WeMos_D1_Mini1.5V, microSD1.VCC, RHT1.Vcc
  N1: WeMos_D1_Mini1.D1, ZS-042_RTC1.SCL
  N2: WeMos_D1_Mini1.D2, ZS-042_RTC1.SDA
  N3: WeMos_D1_Mini1.D4, RHT1.Data-signal
  N4: WeMos_D1_Mini1.D5, microSD1.SCK
  N5: WeMos_D1_Mini1.D6, microSD1.MISO
  N6: WeMos_D1_Mini1.D7, microSD1.MOSI
  N7: WeMos_D1_Mini1.D8, microSD1.CS
  GND: WeMos_D1_Mini1.G, microSD1.GND, ZS-042_RTC1.GND, RHT1.GND_2
